// Logisim project ControlUnit Logic Diagram.circ as structural Verilog
module ControlUnit1 (
  input  JRFlag,
  input  OP5,
  input  OP4,
  input  OP3,
  input  OP2,
  input  OP1,
  input  OP0,
  output RD1,
  output RD0,
  output J,
  output BR,
  output JR,
  output MR,
  output MTR1,
  output MTR0,
  output ALUOP2,
  output ALUOP1,
  output ALUOP0,
  output MW,
  output ALUSrc,
  output RW
);

  wire and_10_out, and_11_out, and_12_out, and_13_out, and_14_out, and_15_out, not_1_out, not_2_out,
       not_3_out, not_4_out, not_5_out, not_6_out, not_7_out, not_8_out, not_9_out, not_10_out, not_11_out,
       not_12_out, not_13_out, not_14_out, not_15_out, not_16_out, not_17_out, not_18_out;

  not not_1 (not_1_out, OP5);
  not not_2 (not_2_out, OP3);
  not not_3 (not_3_out, OP1);
  not not_4 (not_4_out, OP5);
  not not_5 (not_5_out, OP3);
  not not_6 (not_6_out, OP3);
  not not_7 (not_7_out, OP5);
  and and_1 (ALUOP2, OP3, OP2);
  not not_8 (not_8_out, OP2);
  not not_9 (not_9_out, OP1);
  not not_10 (not_10_out, OP1);
  not not_11 (not_11_out, OP3);
  not not_12 (not_12_out, OP2);
  not not_13 (not_13_out, OP1);
  and and_2 (MW, OP5, OP3);
  or or_1 (ALUSrc, OP5, OP3);
  not not_14 (not_14_out, JRFlag);
  not not_15 (not_15_out, OP1);
  not not_16 (not_16_out, OP2);
  not not_17 (not_17_out, OP3);
  not not_18 (not_18_out, OP1);
  and and_3 (RD1, not_1_out, OP1);
  and and_4 (RD0, not_2_out, not_3_out);
  and and_5 (J, not_4_out, OP1);
  and and_6 (BR, not_5_out, OP2);
  and and_7 (MR, OP5, not_6_out);
  and and_8 (MTR1, not_7_out, OP1);
  and and_9 (ALUOP1, not_8_out, not_9_out);
  and and_10 (and_10_out, not_10_out, OP0);
  and and_11 (and_11_out, not_11_out, OP2);
  and and_12 (and_12_out, OP3, not_12_out, not_13_out);
  and and_13 (and_13_out, not_14_out, not_15_out, not_16_out);
  and and_14 (and_14_out, OP0, not_17_out);
  and and_15 (and_15_out, not_18_out, OP3);
  or or_2 (ALUOP0, and_10_out, and_11_out, and_12_out);
  or or_3 (RW, and_13_out, and_14_out, and_15_out);

  assign JR = JRFlag;
  assign MTR0 = OP5;
endmodule

module ControlUnit2 (
  input  JRFlag,
  input  OP5,
  input  OP4,
  input  OP3,
  input  OP2,
  input  OP1,
  input  OP0,
  output ALUSrc,
  output RW
);

  wire and_1_out, and_2_out, and_3_out, not_1_out, not_2_out, not_3_out, not_4_out, not_5_out;

  or or_1 (ALUSrc, OP3, OP5);
  not not_1 (not_1_out, JRFlag);
  not not_2 (not_2_out, OP2);
  not not_3 (not_3_out, OP1);
  not not_4 (not_4_out, OP3);
  not not_5 (not_5_out, OP1);
  and and_1 (and_1_out, not_1_out, not_2_out, not_3_out);
  and and_2 (and_2_out, not_4_out, OP0);
  and and_3 (and_3_out, OP3, not_5_out);
  or or_2 (RW, and_1_out, and_2_out, and_3_out);
endmodule
